# Fritzing sketch HardwareDrawing (saved by Fritzing 0.9.0b)
breadboards: 1

parts:
  IMU1 = Adafruit 10-DOF IMU Breakout
  BATT1 = LiPoly Battery (1300mAh)
  Turnigy_Plush_ESC_30A3 = Turnigy Plush 30A ESC
  JACK1 = 2.1mm DC Barrel Jack
  Brushless_DC_Motor3 = Brushless DC Motor
  Turnigy_Plush_ESC_30A1 = Turnigy Plush 30A ESC
  Brushless_DC_Motor2 = Brushless DC Motor
  Turnigy_Plush_ESC_30A4 = Turnigy Plush 30A ESC
  Brushless_DC_Motor1 = Brushless DC Motor
  Brushless_DC_Motor4 = Brushless DC Motor
  Turnigy_Plush_ESC_30A2 = Turnigy Plush 30A ESC
  BeagleBone1 = BeagleBone Black

nets:
  N1: IMU1.3Vo, BeagleBone1.no_name_yet#3
  N2: IMU1.GND, BeagleBone1.no_name_yet#2
  N3: IMU1.SCL, BeagleBone1.no_name_yet#19
  N4: IMU1.SDA, BeagleBone1.no_name_yet#20
  N5: BATT1.positive, Turnigy_Plush_ESC_30A3.+11_1V, Turnigy_Plush_ESC_30A1.+11_1V, Turnigy_Plush_ESC_30A4.+11_1V, Turnigy_Plush_ESC_30A2.+11_1V
  N6: BATT1.negative, Turnigy_Plush_ESC_30A3.GROUND, Turnigy_Plush_ESC_30A1.GROUND, Turnigy_Plush_ESC_30A4.GROUND, Turnigy_Plush_ESC_30A2.GROUND
  N7: Turnigy_Plush_ESC_30A3.U, Brushless_DC_Motor3.u
  N8: Turnigy_Plush_ESC_30A3.V, Brushless_DC_Motor3.v
  N9: Turnigy_Plush_ESC_30A3.W, Brushless_DC_Motor3.w
  N10: Turnigy_Plush_ESC_30A3.PWM_IN, Turnigy_Plush_ESC_30A3.PWR_OUT, Turnigy_Plush_ESC_30A3.GND, BeagleBone1.no_name_yet#113
  N11: JACK1.center, Turnigy_Plush_ESC_30A1.PWR_OUT
  N12: JACK1.switch, JACK1.sleeve, Turnigy_Plush_ESC_30A1.GND
  N13: Turnigy_Plush_ESC_30A1.U, Brushless_DC_Motor1.u
  N14: Turnigy_Plush_ESC_30A1.V, Brushless_DC_Motor1.v
  N15: Turnigy_Plush_ESC_30A1.W, Brushless_DC_Motor1.w
  N16: Turnigy_Plush_ESC_30A1.PWM_IN, BeagleBone1.no_name_yet#14
  N17: Brushless_DC_Motor2.w, Turnigy_Plush_ESC_30A2.V
  N18: Brushless_DC_Motor2.v, Turnigy_Plush_ESC_30A2.W
  N19: Brushless_DC_Motor2.u, Turnigy_Plush_ESC_30A2.U
  N20: Turnigy_Plush_ESC_30A4.U, Brushless_DC_Motor4.u
  N21: Turnigy_Plush_ESC_30A4.V, Brushless_DC_Motor4.w
  N22: Turnigy_Plush_ESC_30A4.W, Brushless_DC_Motor4.v
  N23: Turnigy_Plush_ESC_30A4.PWM_IN, BeagleBone1.no_name_yet#16
  N24: Turnigy_Plush_ESC_30A2.PWM_IN, Turnigy_Plush_ESC_30A2.PWR_OUT, Turnigy_Plush_ESC_30A2.GND, BeagleBone1.no_name_yet#115, BeagleBone1.no_name_yet#117, BeagleBone1.no_name_yet#119

custom parts:
  LiPoly Battery (1300mAh): Lithium Ion Polymer Battery (1300mAh)
  2.1mm DC Barrel Jack: 2.1mm DC Barrel Jack with Thru-Hole Connectors (breadboardable)
  BeagleBone Black: BeagleBone Black rev. A5B
